# Fritzing sketch Receiver (saved by Fritzing 0.8.5b)
breadboards: 2

parts:
  U1 = atmega328 [package=dip]
  XTAL1 = Crystal [frequency="16 Mhz" package=THT]
  U2 = 2.4GHz Low Power Transceiver [package=qfn20]
  U3 = ATMEGA8U2 [package=tqfp]  # not connected
  X1 = USB Connectors [package=usb-minib-nostop]  # not connected

nets:
  N1: U1.XLAT1, XTAL1.pin_1
  N2: U1.XLAT2, XTAL1.pin_0
  N3: U1.D9_(PWM), U2.CE
  N4: U1.D10_(PWM), U2.CSN
  N5: U1.D11_(PWM), U2.MOSI
  N6: U1.D12, U2.MISO
  N7: U1.D13, U2.SCK
  N8: U1.AVCC, U2.VDD
  N9: U1.GND#21, U2.VSS
