# Fritzing sketch Transmitter (saved by Fritzing 0.8.5b)
breadboards: 2

parts:
  U3 = atmega328 [package=dip]
  XTAL2 = Crystal [frequency="16 Mhz" package=THT]
  U4 = 2.4GHz Low Power Transceiver [package=qfn20]
  S1 = Square Pushbutton
  S2 = Square Pushbutton  # not connected
  S3 = Square Pushbutton  # not connected
  U5 = POT [package=pot_alpha_rv16af-20]
  U6 = LIPO-2000mAh [package=lipo-2000]

nets:
  N1: U3.D2, S1.leg1
  N2: U3.XLAT1, XTAL2.pin_1
  N3: U3.XLAT2, XTAL2.pin_0
  N4: U3.D9_(PWM), U4.CE
  N5: U3.D10_(PWM), U4.CSN
  N6: U3.D11_(PWM), U4.MOSI
  N7: U3.D12, U4.MISO
  N8: U3.D13, U4.SCK
  N9: U3.AVCC, U4.VDD, U5.A, U6.+
  N10: U3.GND#21, U4.VSS, U5.E, U6.-
  N11: U3.A0, U5.S
